# Fritzing sketch bluetooth_setup (saved by Fritzing 0.9.3b)
breadboards: 1

parts:
  Part1 = Bluetooth HC-05 Macho
  R2 = Resistor [tolerance=±5% resistance=2.2k package=THT]  # not connected
  Pro_Micro1 = Pro Micro
  R1 = Resistor [tolerance=±5% resistance=1.1k package=THT]  # not connected
  Part2 = Bluetooth HC-05 Macho

nets:
  N1: Part1.TXD, Pro_Micro1.RX0
  VCC: Part1.VCC, Part1.Key, Part2.VCC
  GND: Part1.GND, Pro_Micro1.GND, Part2.GND

notes:
  S
  M

custom parts:
  Pro Micro: The SparkFun Pro Micro is a complete USB-based microcontoller development system, in a very small footprint, capable of implementing many types of projects. All programming can be done via the USB port.
