# Fritzing sketch robot (saved by Fritzing 0.9.3b)
breadboards: 1

parts:
  Pro_Micro1 = Pro Micro
  IC1 = H-Bridge [package=THT]
  Part1 = Bluetooth HC-05 Macho
  M1 = DC Motor
  M2 = DC Motor
  BATT1 = 4xAA Switchable Battery Pack w/Bare Wire
  R1 = Resistor [tolerance=±5% resistance=1.1k package=THT]  # not connected
  R2 = Resistor [tolerance=±5% resistance=2.2k package=THT]

nets:
  GND: Pro_Micro1.GND, IC1.GND1, IC1.GND2, IC1.GND3, IC1.GND4, Part1.GND, BATT1.NEG, R2.Pin_1
  N1: Pro_Micro1.D2, IC1.1A
  N2: Pro_Micro1.D3, IC1.1_2EN
  N3: Pro_Micro1.D5, IC1.4A
  N4: Pro_Micro1.D7, IC1.2A
  N5: Pro_Micro1.D8, IC1.3A
  N6: Pro_Micro1.D9, IC1.3_4EN
  N7: Pro_Micro1.D16/MOSI, Part1.TXD
  VCC: Pro_Micro1.VCC, IC1.VCC1, Part1.VCC
  N8: Pro_Micro1.RAW, IC1.VCC2, BATT1.POS
  N9: IC1.1Y, M1.pin_2
  N10: IC1.2Y, M1.pin_1
  N11: IC1.3Y, M2.pin_2
  N12: IC1.4Y, M2.pin_1
  N13: Part1.RXD, R2.Pin_0

custom parts:
  Pro Micro: The SparkFun Pro Micro is a complete USB-based microcontoller development system, in a very small footprint, capable of implementing many types of projects. All programming can be done via the USB port.
  4xAA Switchable Battery Pack w/Bare Wire: 4xAA Switchable Battery Pack with Bare Wire connection
